# Fritzing sketch ±5V_3.3V_PowerSupply (saved by Fritzing 0.9.3b)
breadboards: 2

parts:
  U1 = Voltage Regulator - 5V [package="TO220 [THT]"]
  D1 = Rectifier Diode [part_number=1N4001 package="300 mil [THT]"]
  C1 = Ceramic Capacitor [capacitance=100nF package="100 mil [THT, multilayer]"]
  C2 = Ceramic Capacitor [capacitance=100nF package="100 mil [THT, multilayer]"]
  D2 = Rectifier Diode [part_number=1N4001 package="300 mil [THT]"]
  VCC1 = Battery block 9V
  F1 = Resettable Fuse PTC [package=ptc]
  C3 = Electrolytic Capacitor [capacitance=1µF package="100 mil [THT, electrolytic]"]
  D3 = Rectifier Diode [part_number=1N4001 package="300 mil [THT]"]
  R1 = Resistor [tolerance=±5% resistance=1k package=THT]
  LED1 = LED - 3mm [color="Green (555nm)" package="3 mm [THT]"]
  U3 = Voltage Regulator - 5V [package="TO220 [THT]"]
  F2 = Resettable Fuse PTC [package=ptc]
  VCC2 = Battery block 9V
  D4 = Rectifier Diode [part_number=1N4001 package="300 mil [THT]"]
  C4 = Electrolytic Capacitor [capacitance=1µF package="100 mil [THT, electrolytic]"]
  D5 = Rectifier Diode [part_number=1N4001 package="300 mil [THT]"]
  C5 = Ceramic Capacitor [capacitance=100nF package="100 mil [THT, multilayer]"]
  C6 = Ceramic Capacitor [capacitance=100nF package="100 mil [THT, multilayer]"]
  C7 = Electrolytic Capacitor [capacitance=1µF package="100 mil [THT, electrolytic]"]
  R2 = Resistor [tolerance=±5% resistance=1k package=THT]
  LED2 = LED - 3mm [color="Green (555nm)" package="3 mm [THT]"]
  D6 = Rectifier Diode [part_number=1N4001 package="300 mil [THT]"]
  U4 = Voltage Regulator - 5V [package="TO220 [THT]"]
  C8 = Ceramic Capacitor [capacitance=100nF package="100 mil [THT, multilayer]"]
  C9 = Electrolytic Capacitor [capacitance=1µF package="100 mil [THT, electrolytic]"]
  D7 = Rectifier Diode [part_number=1N4001 package="300 mil [THT]"]
  C10 = Electrolytic Capacitor [capacitance=1µF package="100 mil [THT, electrolytic]"]
  C11 = Ceramic Capacitor [capacitance=100nF package="100 mil [THT, multilayer]"]
  D8 = Rectifier Diode [part_number=1N4001 package="300 mil [THT]"]

nets:
  N1: U1.input_voltage, D1.cathode, C1.1, D2.cathode, C3.+
  GND: U1.GND, C1.0, C2.1, VCC1.-, C3.-, D3.anode, R1.Pin_1, U3.input_voltage, VCC2.+, C4.+, C5.0, C6.1, C7.+, R2.Pin_1, D6.cathode, U4.GND, C8.0, C9.-, C10.+, C11.1, D8.anode
  N2: U1.output_voltage, D1.anode, C2.0, D3.cathode, LED1.anode, U4.input_voltage, C8.1, D7.cathode, C10.-
  N3: D2.anode, F1.2
  N4: VCC1.+, F1.1
  N5: R1.Pin_0, LED1.cathode
  N6: U3.GND, D4.anode, C4.-, D5.anode, C5.1
  N7: U3.output_voltage, D5.cathode, C6.0, C7.-, LED2.cathode, D6.anode
  N8: F2.1, VCC2.-
  N9: F2.2, D4.cathode
  N10: R2.Pin_0, LED2.anode
  N11: U4.output_voltage, C9.+, D7.anode, C11.0, D8.cathode

notes:
  GND
  +9V
  GND
  +5V
  -9V
  GND
  -5V
  GND
  +3.3V
